// Digital circuit mips_ULA16bits.dig as structural Verilog
module mips_ULA16bits (
  input  Ainvert,
  input  Binvert,
  input  \Operação ,
  input  CarryIn,
  input  [15:0] A,
  input  [15:0] B,
  output Saida0,
  output Saida1,
  output Saida2,
  output Saida3,
  output Saida4,
  output Saida5,
  output Saida6,
  output Saida7,
  output Saida8,
  output Saida9,
  output Saida10,
  output Saida11,
  output Saida12,
  output Saida13,
  output Saida14,
  output Saida15
);

  wire mips_ula8bits_aberta_1_p7, mips_ula8bits_aberta_1_p16;

  // mips_ULA8bits_aberta mips_ula8bits_aberta_1: pin names not known; wires that end beside it: Ainvert, Binvert, CarryIn, \Operação , A[0], B[0], mips_ula8bits_aberta_1_p7, Saida0, Saida1, Saida2, Saida3, Saida4, Saida5, Saida6, Saida7, mips_ula8bits_aberta_1_p16
  // mips_ULA8bits_aberta mips_ula8bits_aberta_2: pin names not known; wires that end beside it: Ainvert, Binvert, mips_ula8bits_aberta_1_p16, \Operação , A[1], B[1], 1'b0, Saida8, Saida9, Saida10, Saida11, Saida12, Saida13, Saida14, Saida15, mips_ula8bits_aberta_1_p7
endmodule
