// Digital circuit mips_ULA1bit.dig as structural Verilog
module mips_ULA1bit (
  input  A,
  input  B,
  input  CarryIn,
  input  Less,
  input  Ainvert,
  input  Binvert,
  input  [1:0] \Operação ,
  output CarryOut,
  output Resultado
);

  wire and_1_out, mips_mux2_1_saida, mips_mux2_2_saida, mips_somacomplet_1_s, not_1_out, not_2_out, or_1_out;

  not not_1 (not_1_out, A);
  not not_2 (not_2_out, B);
  mips_mux2 mips_mux2_1 (.A(B), .B(not_2_out), .S(Binvert), .Saida(mips_mux2_1_saida));
  mips_mux2 mips_mux2_2 (.A(A), .B(not_1_out), .S(Ainvert), .Saida(mips_mux2_2_saida));
  and and_1 (and_1_out, mips_mux2_2_saida, mips_mux2_1_saida);
  or or_1 (or_1_out, mips_mux2_2_saida, mips_mux2_1_saida);
  mips_somacomplet mips_somacomplet_1 (
    .A(mips_mux2_2_saida), .B(mips_mux2_1_saida), .CarryIn(CarryIn), .S(mips_somacomplet_1_s),
    .CarryOut(CarryOut));
  // mips_mux4 mips_mux4_1: pin names not known; wires that end beside it: and_1_out, or_1_out, mips_somacomplet_1_s, Less, \Operação [0], \Operação [1], Resultado
endmodule
