// Digital circuit mips_ULA32bits.dig as structural Verilog
module mips_ULA32bits (
  input  Ainvert,
  input  Binvert,
  input  \Operação ,
  input  CarryIn,
  input  [31:0] A,
  input  [31:0] B,
  output Saida0,
  output Saida1,
  output Saida2,
  output Saida3,
  output Saida4,
  output Saida5,
  output Saida6,
  output Saida7,
  output Saida8,
  output Saida9,
  output Saida10,
  output Saida11,
  output Saida12,
  output Saida13,
  output Saida14,
  output Saida15,
  output Saida16,
  output Saida17,
  output Saida18,
  output Saida19,
  output Saida20,
  output Saida21,
  output Saida22,
  output Saida23,
  output Saida24,
  output Saida25,
  output Saida26,
  output Saida27,
  output Saida28,
  output Saida29,
  output Saida30,
  output Saida31
);

  wire mips_ula16bits_aberta_1_carryout, mips_ula16bits_aberta_2_carryout;

  mips_ULA16bits_aberta mips_ula16bits_aberta_1 (
    .Ainvert(Ainvert), .Binvert(Binvert), .\Operação (\Operação ), .CarryIn(CarryIn), .A(A[15:0]),
    .B(B[15:0]), .Less(mips_ula16bits_aberta_2_carryout), .Saida0(Saida0), .Saida1(Saida1), .Saida2(Saida2),
    .Saida3(Saida3), .Saida4(Saida4), .Saida5(Saida5), .Saida6(Saida6), .Saida7(Saida7), .Saida8(Saida8),
    .Saida9(Saida9), .Saida10(Saida10), .Saida11(Saida11), .Saida12(Saida12), .Saida13(Saida13),
    .Saida14(Saida14), .Saida15(Saida15), .CarryOut(mips_ula16bits_aberta_1_carryout));
  mips_ULA16bits_aberta mips_ula16bits_aberta_2 (
    .Ainvert(Ainvert), .Binvert(Binvert), .\Operação (\Operação ),
    .CarryIn(mips_ula16bits_aberta_1_carryout), .A(A[31:16]), .B(B[31:16]), .Less(1'b0), .Saida0(Saida16),
    .Saida1(Saida17), .Saida2(Saida18), .Saida3(Saida19), .Saida4(Saida20), .Saida5(Saida21),
    .Saida6(Saida22), .Saida7(Saida23), .Saida8(Saida24), .Saida9(Saida25), .Saida10(Saida26),
    .Saida11(Saida27), .Saida12(Saida28), .Saida13(Saida29), .Saida14(Saida30), .Saida15(Saida31),
    .CarryOut(mips_ula16bits_aberta_2_carryout));
endmodule
