// Digital circuit mips_ULA4bits.dig as structural Verilog
module mips_ULA4bits (
  input  Binvert,
  input  Ainvert,
  input  CarryIn,
  input  [1:0] \Operação ,
  input  [3:0] A,
  input  [3:0] B,
  output Result0,
  output Result1,
  output Result2,
  output Result3
);

  wire mips_ula1bit_1_carryout, mips_ula1bit_2_carryout, mips_ula1bit_3_carryout, mips_ula1bit_4_carryout;

  mips_ULA1bit mips_ula1bit_1 (
    .A(A[0]), .B(B[0]), .CarryIn(CarryIn), .Less(mips_ula1bit_4_carryout), .Ainvert(Ainvert),
    .Binvert(Binvert), .\Operação (\Operação ), .CarryOut(mips_ula1bit_1_carryout), .Resultado(Result0));
  mips_ULA1bit mips_ula1bit_2 (
    .A(A[1]), .B(B[1]), .CarryIn(mips_ula1bit_1_carryout), .Less(1'b0), .Ainvert(Ainvert), .Binvert(Binvert),
    .\Operação (\Operação ), .CarryOut(mips_ula1bit_2_carryout), .Resultado(Result1));
  mips_ULA1bit mips_ula1bit_3 (
    .A(A[2]), .B(B[2]), .CarryIn(mips_ula1bit_2_carryout), .Less(1'b0), .Ainvert(Ainvert), .Binvert(Binvert),
    .\Operação (\Operação ), .CarryOut(mips_ula1bit_3_carryout), .Resultado(Result2));
  mips_ULA1bit mips_ula1bit_4 (
    .A(A[3]), .B(B[3]), .CarryIn(mips_ula1bit_3_carryout), .Less(1'b0), .Ainvert(Ainvert), .Binvert(Binvert),
    .\Operação (\Operação ), .CarryOut(mips_ula1bit_4_carryout), .Resultado(Result3));
endmodule
