// Digital circuit mips_ULA8bits.dig as structural Verilog
module mips_ULA8bits (
  input  A0,
  input  B0,
  input  A1,
  input  B1,
  input  A2,
  input  B2,
  input  A3,
  input  B3,
  input  A4,
  input  B4,
  input  A5,
  input  B5,
  input  A6,
  input  B6,
  input  A7,
  input  B7,
  input  Ainvert,
  input  Binvert,
  input  CarryIn,
  input  [1:0] \Operação ,
  output Saida0,
  output Saida1,
  output Saida2,
  output Saida3,
  output Saida4,
  output Saida5,
  output Saida6,
  output Saida7
);

  wire mips_ula4bits_aberta_1_carryout, mips_ula4bits_aberta_2_carryout;

  mips_ULA4bits_aberta mips_ula4bits_aberta_1 (
    .A0(A0), .B0(B0), .Binvert(Binvert), .Ainvert(Ainvert), .CarryIn(CarryIn), .\Operação (\Operação ),
    .A1(A1), .B1(B1), .A2(A2), .B2(B2), .A3(A3), .B3(B3), .Less(mips_ula4bits_aberta_2_carryout),
    .Result0(Saida0), .Result1(Saida1), .Result2(Saida2), .Result3(Saida3),
    .CarryOut(mips_ula4bits_aberta_1_carryout));
  mips_ULA4bits_aberta mips_ula4bits_aberta_2 (
    .A0(A4), .B0(B4), .Binvert(Binvert), .Ainvert(Ainvert), .CarryIn(mips_ula4bits_aberta_1_carryout),
    .\Operação (\Operação ), .A1(A5), .B1(B5), .A2(A6), .B2(B6), .A3(A7), .B3(B7), .Less(1'b0),
    .Result0(Saida4), .Result1(Saida5), .Result2(Saida6), .Result3(Saida7),
    .CarryOut(mips_ula4bits_aberta_2_carryout));
  // Pins of 1 and 2 bits meet at \Operação 
endmodule
