// Digital circuit mips_bancodeReg.dig as structural Verilog
module mips_bancodeReg (
);

  mips_decodificador mips_decodificador_1 ();  // open: Entrada, Saida0, Saida1, Saida2, Saida3, Saida4, Saida5, Saida6, Saida7, Saida8, Saida9, Saida10, Saida11, Saida12, Saida13, Saida14, Saida15, Saida16, Saida17, Saida18, Saida19, Saida20, Saida21, Saida22, Saida23, Saida24, Saida25, Saida26, Saida27, Saida28, Saida29, Saida30, Saida31
  mips_reg32bits mips_reg32bits_1 ();  // open: Entrada, Clock, Saida
  mips_mux32 mips_mux32_1 ();  // open: S0, S1, S2, S3, S4, Entrada, Saida
endmodule
