// Digital circuit mips_mux4_new_32bits.dig as structural Verilog
module mips_mux4_new_32bits (
  input  [31:0] A,
  input  [31:0] B,
  input  [31:0] C,
  input  [31:0] D,
  input  S0,
  input  S1,
  output [31:0] Saida
);

  wire mips_mux2_1_p4, mips_mux2_2_p4;

  // mips_mux2 mips_mux2_1: pin names not known; wires that end beside it: A, B, S0, mips_mux2_1_p4, Saida
  // mips_mux2 mips_mux2_2: pin names not known; wires that end beside it: C, D, S0, mips_mux2_2_p4
  mips_mux2 mips_mux2_3 (.Entrada0(mips_mux2_1_p4), .Entrada1(mips_mux2_2_p4), .\Seleção (S1));  // open: Saida
endmodule
